# Fritzing sketch Schaltplan_Tischkicker (saved by Fritzing 0.9.3b)
breadboards: 2

parts:
  7_Segment1 = 7 Segment Display
  7_Segment2 = 7 Segment Display
  7_Segment3 = 7 Segment Display
  7_Segment4 = 7 Segment Display
  R1 = Photocell (LDR) [package=THT]
  R2 = Photocell (LDR) [package=THT]
  LED1 = LED - 5mm [color="Red (633nm)" package="5 mm [THT]"]
  LED2 = LED - 5mm [color="Red (633nm)" package="5 mm [THT]"]
  Reset = Pushbutton [package="[THT]"]
  R3 = Resistor [tolerance=±5% resistance=220 package=THT]
  R4 = Resistor [tolerance=±5% resistance=220 package=THT]
  R5 = Resistor [tolerance=±5% resistance=220 package=THT]
  R6 = Resistor [tolerance=±5% resistance=220 package=THT]
  Q1 = NPN-Transistor [package="TO92 [THT]"]
  Q2 = NPN-Transistor [package="TO92 [THT]"]
  Q3 = NPN-Transistor [package="TO92 [THT]"]
  Q4 = NPN-Transistor [package="TO92 [THT]"]
  Power_plug1 = Power plug
  R7 = Resistor [tolerance=±5% resistance=220 package=THT]
  R8 = Resistor [tolerance=±5% resistance=220 package=THT]
  R9 = Resistor [tolerance=±5% resistance=220 package=THT]
  R10 = Resistor [tolerance=±5% resistance=220 package=THT]
  R11 = Resistor [tolerance=±5% resistance=220 package=THT]
  ESP_VIN_bis_EN = female pin header, 15 pins [form="♀ (female)"]
  ESP_3V3_bis_D23 = female pin header, 15 pins [form="♀ (female)"]

nets:
  N1: 7_Segment1.Segment_E, 7_Segment2.Segment_E, 7_Segment3.Segment_E, 7_Segment4.Segment_E, ESP_3V3_bis_D23.pin3
  N2: 7_Segment1.Segment_D, 7_Segment2.Segment_D, 7_Segment3.Segment_D, 7_Segment4.Segment_D, ESP_3V3_bis_D23.pin4
  N3: 7_Segment1.common_cathode, Q2.E
  N4: 7_Segment1.Segment_C, 7_Segment2.Segment_C, 7_Segment3.Segment_C, 7_Segment4.Segment_C, ESP_3V3_bis_D23.pin5
  N5: 7_Segment1.Segment_DP, 7_Segment2.Segment_DP, 7_Segment3.Segment_DP, 7_Segment4.Segment_DP, ESP_3V3_bis_D23.pin8
  N6: 7_Segment1.Segment_B, 7_Segment2.Segment_B, 7_Segment3.Segment_B, 7_Segment4.Segment_B, ESP_3V3_bis_D23.pin14
  N7: 7_Segment1.Segment_A, 7_Segment2.Segment_A, 7_Segment3.Segment_A, 7_Segment4.Segment_A, ESP_3V3_bis_D23.pin11
  N8: 7_Segment1.Segment_F, 7_Segment2.Segment_F, 7_Segment3.Segment_F, 7_Segment4.Segment_F, ESP_3V3_bis_D23.pin10
  N9: 7_Segment1.Segment_G, 7_Segment2.Segment_G, 7_Segment3.Segment_G, 7_Segment4.Segment_G, ESP_3V3_bis_D23.pin9
  N10: 7_Segment2.common_cathode, Q3.E
  N11: 7_Segment3.common_cathode, Q4.E
  N12: 7_Segment4.common_cathode, Q1.E
  5V: R1.pin_0, R2.pin_0, Reset.Pin_1, Reset.Pin_2, R3.Pin_1, R4.Pin_1, Power_plug1.VCC, ESP_VIN_bis_EN.pin1
  N13: R1.pin_1, R5.Pin_0, ESP_VIN_bis_EN.pin4
  N14: R2.pin_1, R6.Pin_0, ESP_VIN_bis_EN.pin5
  GND: LED1.cathode, LED2.cathode, R5.Pin_1, R6.Pin_1, Q1.C, Q2.C, Q3.C, Q4.C, Power_plug1.GND, R11.Pin_0, ESP_VIN_bis_EN.pin2
  N15: LED1.anode, R4.Pin_0
  N16: LED2.anode, R3.Pin_0
  N17: Reset.Pin_3, Reset.Pin_4, R11.Pin_1, ESP_VIN_bis_EN.pin3
  N18: Q1.B, R10.Pin_0
  N19: Q2.B, R9.Pin_0
  N20: Q3.B, R8.Pin_0
  N21: Q4.B, R7.Pin_0
  N22: R7.Pin_1, ESP_VIN_bis_EN.pin8
  N23: R8.Pin_1, ESP_VIN_bis_EN.pin9
  N24: R9.Pin_1, ESP_VIN_bis_EN.pin6
  N25: R10.Pin_1, ESP_VIN_bis_EN.pin7
